// Logisim project Bcd_adder_subtractor.circ as structural Verilog: 2 circuits, main circuit adder
module adder (
  input  Cin,
  input  A,
  input  B,
  output S,
  output Cout
);

  wire and_1_out, and_2_out, xor_1_out;

  xor xor_1 (xor_1_out, A, B);
  xor xor_2 (S, xor_1_out, Cin);
  and and_1 (and_1_out, Cin, xor_1_out);
  and and_2 (and_2_out, A, B);
  or or_1 (Cout, and_1_out, and_2_out);
endmodule

module bcd (
  input  in_1,
  input  [3:0] A,
  input  [3:0] B,
  output [3:0] out_4,
  output carry
);

  wire adder_1_cout, adder_1_s, adder_2_cout, adder_2_s, adder_3_cout, adder_3_s, adder_4_cout, adder_4_s,
       adder_5_cout, adder_6_cout, adder_7_cout, and_1_out, and_2_out;

  adder adder_1 (.Cin(in_1), .A(A[0]), .B(B[0]), .S(adder_1_s), .Cout(adder_1_cout));
  adder adder_2 (.Cin(adder_1_cout), .A(A[1]), .B(B[1]), .S(adder_2_s), .Cout(adder_2_cout));
  adder adder_3 (.Cin(adder_2_cout), .A(A[2]), .B(B[2]), .S(adder_3_s), .Cout(adder_3_cout));
  adder adder_4 (.Cin(adder_3_cout), .A(A[3]), .B(B[3]), .S(adder_4_s), .Cout(adder_4_cout));
  and and_1 (and_1_out, adder_2_s, adder_4_s);
  and and_2 (and_2_out, adder_3_s, adder_4_s);
  adder adder_5 (.Cin(in_1), .A(1'b0), .B(adder_1_s), .S(out_4[0]), .Cout(adder_5_cout));
  adder adder_6 (.Cin(adder_5_cout), .A(carry), .B(adder_2_s), .S(out_4[1]), .Cout(adder_6_cout));
  adder adder_7 (.Cin(adder_6_cout), .A(carry), .B(adder_3_s), .S(out_4[2]), .Cout(adder_7_cout));
  adder adder_8 (.Cin(adder_7_cout), .A(1'b0), .B(adder_4_s), .S(out_4[3]));  // open: Cout
  or or_1 (carry, and_1_out, and_2_out, adder_4_cout);

  // Notes on the sheet:
  //   Z1
  //   Md Mushfiq Fuad
  //   Z2
  //   Z3
  //   Z4
  //   1410083042
  //   BCD ADDER
  //   S1
  //   S2
  //   S3
  //   S4
endmodule
