// Logisim project Binary_to_Excess-3.circ as structural Verilog: 1 circuit, main circuit main
// W
module main (
  input  W,
  input  X,
  input  Y,
  input  Z,
  output A,
  output B,
  output C,
  output D
);

  wire nand_1_out, nand_2_out, nand_4_out, nand_5_out, nand_6_out, nand_7_out, nand_8_out, nand_9_out,
       nand_10_out, nand_11_out;

  nand nand_1 (nand_1_out, X, X);
  nand nand_2 (nand_2_out, Y, Y);
  nand nand_3 (D, Z, Z);
  nand nand_4 (nand_4_out, W, W);
  nand nand_5 (nand_5_out, X, Z);
  nand nand_6 (nand_6_out, X, Y);
  nand nand_7 (nand_7_out, X, nand_1_out, D);
  nand nand_8 (nand_8_out, nand_1_out, Z);
  nand nand_9 (nand_9_out, nand_1_out, Y);
  nand nand_10 (nand_10_out, nand_2_out, D);
  nand nand_11 (nand_11_out, Y, Z);
  nand nand_12 (A, nand_4_out, nand_5_out, nand_6_out);
  nand nand_13 (B, nand_7_out, nand_8_out, nand_9_out);
  nand nand_14 (C, nand_10_out, nand_11_out);

  // Notes on the sheet:
  //   Md Mushfiq Fuad
  //   1410083042
endmodule
