// Logisim project combinational_new.circ as structural Verilog: 2 circuits, main circuit main
module main (
  input  A,
  input  B,
  input  C
);

  wire B_prime_C_out, BC_prime_out, not_1_out, not_2_out, not_3_out, not_4_out, or_1_out, or_2_out, or_3_out;

  not not_1 (not_1_out, C);
  not not_2 (not_2_out, B);
  or or_1 (or_1_out, C, B);
  not not_3 (not_3_out, B);
  and B_prime_C (B_prime_C_out, not_3_out, C);
  and BC_prime (BC_prime_out, B, not_4_out);
  not not_4 (not_4_out, C);
  or or_2 (or_2_out, not_1_out, not_2_out);
  or or_3 (or_3_out, B_prime_C_out, BC_prime_out, A);
  _7_Segment_Display u_7_segment_display_1 (
    .f(or_2_out), .a(or_3_out), .b(C), .e(or_2_out), .d(or_2_out), .c(or_1_out));  // open: g, dp
endmodule

module sequential (
  input  C,
  input  B,
  input  A
);

  wire A_q, A_qn, and_1_out, B_prime_C_2_out, B_prime_C_out, B_q, B_qn, BC_out, BC_prime_2_out, BC_prime_out,
       C_q, C_qn, clock_1_out, not_1_out, not_2_out, not_3_out, not_4_out, or_1_out, or_2_out, or_3_out,
       or_4_out;

  and BC (BC_out, B_q, C_q);
  and BC_prime (BC_prime_out, C_q, B_qn);
  or or_1 (or_1_out, BC_prime_out, B_prime_C_out);
  and B_prime_C (B_prime_C_out, C_qn, B_q);
  and and_1 (and_1_out, A_qn, C_qn);
  Clock clock_1 (.out(clock_1_out));
  not not_1 (not_1_out, C_q);
  not not_2 (not_2_out, B_q);
  D_Flip_Flop u_A (.clk(clock_1_out), .D(BC_out), .Q(A_q), .Qn(A_qn));  // open: preset, en, reset
  D_Flip_Flop u_B (.clk(clock_1_out), .D(or_1_out), .Q(B_q), .Qn(B_qn));  // open: preset, en, reset
  D_Flip_Flop u_C (.clk(clock_1_out), .D(and_1_out), .Q(C_q), .Qn(C_qn));  // open: preset, en, reset
  or or_2 (or_2_out, C_q, B_q);
  not not_3 (not_3_out, B_q);
  and B_prime_C_2 (B_prime_C_2_out, not_3_out, C_q);
  and BC_prime_2 (BC_prime_2_out, B_q, not_4_out);
  not not_4 (not_4_out, C_q);
  or or_3 (or_3_out, not_1_out, not_2_out);
  or or_4 (or_4_out, B_prime_C_2_out, BC_prime_2_out, A_q);
  _7_Segment_Display u_7_segment_display_1 (
    .f(or_3_out), .a(or_4_out), .b(C_q), .e(or_3_out), .d(or_3_out), .c(or_2_out));  // open: g, dp
endmodule
