// Logisim project seven_segment.circ as structural Verilog: 1 circuit, main circuit seven_segment
module seven_segment (
  input  A,
  input  B,
  input  C,
  input  D
);

  wire B_prime_C_out, B_prime_D_prime_out, BC_prime_D_out, BC_prime_out, BD_out, BD_prime_out,
       C_prime_D_prime_out, CD_out, CD_prime_out, not_1_out, not_2_out, not_3_out, not_4_out, or_1_out,
       or_2_out, or_3_out, or_4_out, or_5_out, or_6_out, or_7_out;

  not not_1 (not_1_out, B);
  not not_2 (not_2_out, D);
  and B_prime_D_prime (B_prime_D_prime_out, not_1_out, not_2_out);
  and BD (BD_out, B, D);
  not not_3 (not_3_out, C);
  not not_4 (not_4_out, B);
  and CD (CD_out, C, D);
  and C_prime_D_prime (C_prime_D_prime_out, not_3_out, not_2_out);
  and B_prime_C (B_prime_C_out, not_1_out, C);
  and CD_prime (CD_prime_out, C, not_2_out);
  and BC_prime_D (BC_prime_D_out, B, not_3_out, D);
  and BC_prime (BC_prime_out, not_3_out, B);
  and BD_prime (BD_prime_out, B, not_2_out);
  or or_1 (or_1_out, B, not_3_out, D);
  or or_2 (or_2_out, A, B_prime_D_prime_out, B_prime_C_out, CD_prime_out, BC_prime_D_out);
  or or_3 (or_3_out, A, C, B_prime_D_prime_out, BD_out);
  or or_4 (or_4_out, not_4_out, CD_out, C_prime_D_prime_out);
  or or_5 (or_5_out, B_prime_D_prime_out, CD_prime_out);
  or or_6 (or_6_out, A, C_prime_D_prime_out, BC_prime_out, BD_prime_out);
  or or_7 (or_7_out, A, BC_prime_out, B_prime_C_out, CD_prime_out);
  _7_Segment_Display u_7_segment_display_1 (
    .g(or_7_out), .f(or_6_out), .a(or_3_out), .b(or_4_out), .e(or_5_out), .d(or_2_out), .c(or_1_out));  // open: dp

  // Notes on the sheet:
  //   MD MUSHFIQ FUAD
  //   1410083042
  //   a
  //   f
  //   g
  //   e
  //   d
  //   b
  //   c
endmodule
